# Fritzing sketch reader-schematic (saved by Fritzing 0.9.6b)
breadboards: 1

parts:
  T1 = LM35 Temperature Sensor [package="TO92 [THT]"]
  Part1 = Arduino Uno (Rev3) - ICSP
  R1 = Photocell (LDR) [package=THT]
  R2 = Resistor [tolerance=±5% power=0.25 resistance=10k package=THT]
  RHT1 = Humidity and Temperature Sensor RHT03
  R3 = Resistor [tolerance=±5% power=0.25 resistance=10k package=THT]

nets:
  5V: T1.+Vs, Part1.5V, R1.pin_1, RHT1.Vcc, R3.Pin_1
  N1: T1.Vout, Part1.A5/SCL
  GND: T1.GND, Part1.A0, Part1.GND, R2.Pin_1, RHT1.GND_2
  N2: Part1.D4, RHT1.Data-signal, R3.Pin_0
  N3: R1.pin_0, R2.Pin_0
